// Logisim project cpu.circ as structural Verilog: 19 circuits, main circuit Computer
module Computer (
  input  reset
);

  wire clk, cpu_1_writem;
  wire [14:0] cpu_1_addressm, cpu_1_pc;
  wire [15:0] cpu_1_outm, memory_1_out, rom_1_data, undriven;

  Clock clock_1 (.out(clk));
  ROM #(.addrWidth(15), .dataWidth(16)) rom_1 (.addr(cpu_1_pc), .data(rom_1_data));  // open: sel
  Keyboard keyboard_1 (.clk(clk));  // open: re, clr, avail, data
  CPU cpu_1 (
    .inM(memory_1_out), .instruction(rom_1_data), .reset(reset), .clk(clk), .outM(cpu_1_outm),
    .writeM(cpu_1_writem), .addressM(cpu_1_addressm), .pc(cpu_1_pc));
  Memory memory_1 (
    .in(cpu_1_outm), .outKeyboard(undriven), .clk(clk), .load(cpu_1_writem), .address(cpu_1_addressm),
    .out(memory_1_out));
endmodule

// And
module And16 (
  input  [15:0] a,
  input  [15:0] b,
  output [15:0] out_3
);

  and and_1 (out_3[0], a[0], b[0]);
  and and_2 (out_3[1], a[1], b[1]);
  and and_3 (out_3[2], a[2], b[2]);
  and and_4 (out_3[3], a[3], b[3]);
  and and_5 (out_3[4], a[4], b[4]);
  and and_6 (out_3[5], a[5], b[5]);
  and and_7 (out_3[6], a[6], b[6]);
  and and_8 (out_3[7], a[7], b[7]);
  and and_9 (out_3[8], a[8], b[8]);
  and and_10 (out_3[9], a[9], b[9]);
  and and_11 (out_3[10], a[10], b[10]);
  and and_12 (out_3[11], a[11], b[11]);
  and and_13 (out_3[12], a[12], b[12]);
  and and_14 (out_3[13], a[13], b[13]);
  and and_15 (out_3[14], a[14], b[14]);
  and and_16 (out_3[15], a[15], b[15]);

  // Other names for the same wires on the sheet: out0 = out_3[0]; out1 = out_3[1]; out2 = out_3[2]; out3 = out_3[3];
  //   out4 = out_3[4]; out5 = out_3[5]; out6 = out_3[6]; out7 = out_3[7]; out8 = out_3[8]; out9 = out_3[9];
  //   out10 = out_3[10]; out11 = out_3[11]; out12 = out_3[12]; out13 = out_3[13]; out14 = out_3[14];
  //   out15 = out_3[15]
endmodule

// Not
module Not16 (
  input  [15:0] a,
  output [15:0] out_2
);

  not not_1 (out_2[0], a[0]);
  not not_2 (out_2[1], a[1]);
  not not_3 (out_2[2], a[2]);
  not not_4 (out_2[3], a[3]);
  not not_5 (out_2[4], a[4]);
  not not_6 (out_2[5], a[5]);
  not not_7 (out_2[6], a[6]);
  not not_8 (out_2[7], a[7]);
  not not_9 (out_2[8], a[8]);
  not not_10 (out_2[9], a[9]);
  not not_11 (out_2[10], a[10]);
  not not_12 (out_2[11], a[11]);
  not not_13 (out_2[12], a[12]);
  not not_14 (out_2[13], a[13]);
  not not_15 (out_2[14], a[14]);
  not not_16 (out_2[15], a[15]);

  // Other names for the same wires on the sheet: out0 = out_2[0]; out1 = out_2[1]; out2 = out_2[2]; out3 = out_2[3];
  //   out4 = out_2[4]; out5 = out_2[5]; out6 = out_2[6]; out7 = out_2[7]; out8 = out_2[8]; out9 = out_2[9];
  //   out10 = out_2[10]; out11 = out_2[11]; out12 = out_2[12]; out13 = out_2[13]; out14 = out_2[14];
  //   out15 = out_2[15]
endmodule

module Or16 (
  input  [15:0] a,
  input  [15:0] b,
  output [15:0] out_3
);

  or or_1 (out_3[0], a[0], b[0]);
  or or_2 (out_3[1], a[1], b[1]);
  or or_3 (out_3[2], a[2], b[2]);
  or or_4 (out_3[3], a[3], b[3]);
  or or_5 (out_3[4], a[4], b[4]);
  or or_6 (out_3[5], a[5], b[5]);
  or or_7 (out_3[6], a[6], b[6]);
  or or_8 (out_3[7], a[7], b[7]);
  or or_9 (out_3[8], a[8], b[8]);
  or or_10 (out_3[9], a[9], b[9]);
  or or_11 (out_3[10], a[10], b[10]);
  or or_12 (out_3[11], a[11], b[11]);
  or or_13 (out_3[12], a[12], b[12]);
  or or_14 (out_3[13], a[13], b[13]);
  or or_15 (out_3[14], a[14], b[14]);
  or or_16 (out_3[15], a[15], b[15]);

  // Other names for the same wires on the sheet: out0 = out_3[0]; out1 = out_3[1]; out2 = out_3[2]; out3 = out_3[3];
  //   out4 = out_3[4]; out5 = out_3[5]; out6 = out_3[6]; out7 = out_3[7]; out8 = out_3[8]; out9 = out_3[9];
  //   out10 = out_3[10]; out11 = out_3[11]; out12 = out_3[12]; out13 = out_3[13]; out14 = out_3[14];
  //   out15 = out_3[15]
endmodule

// Mux
module Mux16 (
  input  [15:0] a,
  input  [15:0] b,
  input  sel,
  output [15:0] out_4
);

  Multiplexer #(.width(16), .enable("false")) multiplexer_1 (.in0(a), .in1(b), .out(out_4), .sel(sel));
endmodule

// Or
module Or8Way (
  input  [7:0] in,
  output out
);

  or or_1 (out, in[0], in[1], in[2], in[3], in[4], in[5], in[6], in[7]);
endmodule

module Mux4Way16 (
  input  [15:0] a,
  input  [15:0] b,
  input  [15:0] c,
  input  [15:0] d,
  input  [1:0] sel,
  output [15:0] out
);

  wire [15:0] mux16_1_out_4, mux16_2_out_4;

  Mux16 mux16_1 (.a(a), .b(b), .sel(sel[0]), .out_4(mux16_1_out_4));
  Mux16 mux16_2 (.a(c), .b(d), .sel(sel[0]), .out_4(mux16_2_out_4));
  Mux16 mux16_3 (.a(mux16_1_out_4), .b(mux16_2_out_4), .sel(sel[1]), .out_4(out));
endmodule

module Mux8Way16 (
  input  [15:0] a,
  input  [15:0] b,
  input  [15:0] c,
  input  [15:0] d,
  input  [15:0] e,
  input  [15:0] f,
  input  [15:0] g,
  input  [15:0] h,
  input  [2:0] sel,
  output [15:0] out
);

  wire [15:0] mux4way16_1_out, mux4way16_2_out;

  Mux4Way16 mux4way16_1 (.a(a), .b(b), .c(c), .d(d), .sel(sel[1:0]), .out(mux4way16_1_out));
  Mux4Way16 mux4way16_2 (.a(e), .b(f), .c(g), .d(h), .sel(sel[1:0]), .out(mux4way16_2_out));
  Mux16 mux16_1 (.a(mux4way16_1_out), .b(mux4way16_2_out), .sel(sel[2]), .out_4(out));
endmodule

module DMux4Way (
  input  in,
  input  [1:0] sel,
  output a,
  output b,
  output c,
  output d
);

  Demultiplexer #(.select(2), .enable("false")) demultiplexer_1 (
    .out0(a), .out1(b), .out2(c), .out3(d), .in(in), .sel(sel));
endmodule

module DMux8Way (
  input  in,
  input  [2:0] sel,
  output a,
  output b,
  output c,
  output d,
  output e,
  output f,
  output g,
  output h
);

  wire demultiplexer_1_out0, demultiplexer_1_out1;

  Demultiplexer #(.enable("false")) demultiplexer_1 (
    .out0(demultiplexer_1_out0), .out1(demultiplexer_1_out1), .in(in), .sel(sel[2]));
  DMux4Way dmux4way_1 (.in(demultiplexer_1_out0), .sel(sel[1:0]), .a(a), .b(b), .c(c), .d(d));
  DMux4Way dmux4way_2 (.in(demultiplexer_1_out1), .sel(sel[1:0]), .a(e), .b(f), .c(g), .d(h));
endmodule

module HalfAdder (
  input  a,
  input  b,
  output sum,
  output carry
);

  xor xor_1 (sum, a, b);
  and and_1 (carry, a, b);
endmodule

module FullAdder (
  input  a,
  input  b,
  input  c,
  output sum,
  output carry
);

  wire halfadder_1_carry, halfadder_1_sum, halfadder_2_carry;

  HalfAdder halfadder_1 (.a(a), .b(b), .sum(halfadder_1_sum), .carry(halfadder_1_carry));
  HalfAdder halfadder_2 (.a(halfadder_1_sum), .b(c), .sum(sum), .carry(halfadder_2_carry));
  or or_1 (carry, halfadder_2_carry, halfadder_1_carry);
endmodule

// Add
module Add16 (
  input  [15:0] a,
  input  [15:0] b,
  output [15:0] out_3
);

  Adder #(.width(16)) adder_1 (.a(a), .b(b), .out(out_3));  // open: cin, cout
endmodule

module Inc16 (
  input  [15:0] in,
  output [15:0] out_2
);

  Add16 add16_1 (.a(in), .b(16'h1), .out_3(out_2));
endmodule

module ALU (
  input  [15:0] x,
  input  [15:0] y,
  input  zx,
  input  nx,
  input  zy,
  input  ny,
  input  f,
  input  no,
  output [15:0] out,
  output zr,
  output ng
);

  wire or8way_1_out, or8way_2_out;
  wire [15:0] add16_1_out_3, and16_1_out_3, mux16_1_out_4, mux16_2_out_4, mux16_3_out_4, mux16_4_out_4,
       mux16_5_out_4, not16_1_out_2, not16_2_out_2, not16_3_out_2;

  Mux16 mux16_1 (.a(x), .b({16{1'b0}}), .sel(zx), .out_4(mux16_1_out_4));
  Not16 not16_1 (.a(mux16_1_out_4), .out_2(not16_1_out_2));
  Not16 not16_2 (.a(mux16_2_out_4), .out_2(not16_2_out_2));
  Mux16 mux16_2 (.a(y), .b({16{1'b0}}), .sel(zy), .out_4(mux16_2_out_4));
  Mux16 mux16_3 (.a(mux16_1_out_4), .b(not16_1_out_2), .sel(nx), .out_4(mux16_3_out_4));
  Mux16 mux16_4 (.a(mux16_2_out_4), .b(not16_2_out_2), .sel(ny), .out_4(mux16_4_out_4));
  And16 and16_1 (.a(mux16_3_out_4), .b(mux16_4_out_4), .out_3(and16_1_out_3));
  Add16 add16_1 (.a(mux16_3_out_4), .b(mux16_4_out_4), .out_3(add16_1_out_3));
  Mux16 mux16_5 (.a(and16_1_out_3), .b(add16_1_out_3), .sel(f), .out_4(mux16_5_out_4));
  Mux16 mux16_6 (.a(mux16_5_out_4), .b(not16_3_out_2), .sel(no), .out_4({ng, out[14:0]}));
  Not16 not16_3 (.a(mux16_5_out_4), .out_2(not16_3_out_2));
  Or8Way or8way_1 (.in(out[7:0]), .out(or8way_1_out));
  Or8Way or8way_2 (.in({ng, out[14:8]}), .out(or8way_2_out));
  nor nor_1 (zr, or8way_1_out, or8way_2_out);

  assign out[15] = ng;

  // Notes on the sheet:
  //   x input
  //   y input
endmodule

module Register (
  input  [15:0] in,
  input  load,
  input  clk,
  output [15:0] out
);

  Register_part #(.width(16)) register_1 (.D(in), .en(load), .Q(out), .clk(clk));  // open: clr
endmodule

module PC (
  input  [15:0] in,
  input  load,
  input  inc,
  input  reset,
  input  clk,
  output [15:0] out
);

  wire or_1_out;
  wire [15:0] Mux_2_out_4, Mux_3_out_4, Mux_out_4, plus_1_out_2;

  or or_1 (or_1_out, load, inc, reset);
  Register register_1 (.in(Mux_3_out_4), .load(or_1_out), .clk(clk), .out(out));
  Inc16 plus_1 (.in(out), .out_2(plus_1_out_2));
  Mux16 Mux (.a(out), .b(plus_1_out_2), .sel(inc), .out_4(Mux_out_4));
  Mux16 Mux_2 (.a(Mux_out_4), .b(in), .sel(load), .out_4(Mux_2_out_4));
  Mux16 Mux_3 (.a(Mux_2_out_4), .b({16{1'b0}}), .sel(reset), .out_4(Mux_3_out_4));
endmodule

module CPU (
  input  reset,
  input  clk,
  input  [15:0] inM,
  input  [15:0] instruction,
  output [15:0] outM,
  output writeM,
  output [14:0] addressM,
  output [14:0] pc
);

  wire and_2_out, and_3_out, and_4_out, isCinstruction, isJump__unused, isPositive__unused, loadA, loadD,
       loadPC, ng, not_2_out, not_3_out, PCinc, selInstrOrALU, zr;
  wire [15:0] mux16_1_out_4, outAorM, outDReg;
  wire [15:15] outAReg, outPC;

  Mux16 mux16_1 (.a(instruction), .b(outM), .sel(selInstrOrALU), .out_4(mux16_1_out_4));
  not not_1 (isCinstruction, instruction[15]);
  Register A (.in(mux16_1_out_4), .load(loadA), .clk(clk), .out({outAReg[15], addressM}));
  Register D (.in(outM), .load(loadD), .clk(clk), .out(outDReg));
  PC pc_1 (.in({outAReg[15], addressM}), .load(loadPC), .inc(PCinc), .reset(reset), .clk(clk), .out({outPC[15], pc}));
  Mux16 mux16_2 (.a({outAReg[15], addressM}), .b(inM), .sel(instruction[12]), .out_4(outAorM));
  not not_2 (not_2_out, zr);
  and and_1 (isPositive__unused, not_2_out, not_3_out);
  not not_3 (not_3_out, ng);
  and and_2 (and_2_out, isPositive__unused, instruction[0]);
  and and_3 (and_3_out, zr, instruction[1]);
  and and_4 (and_4_out, ng, instruction[2]);
  and and_5 (selInstrOrALU, instruction[5], isCinstruction);
  and and_6 (loadD, instruction[4], isCinstruction);
  and and_7 (writeM, isCinstruction, instruction[3]);
  or or_1 (isJump__unused, and_2_out, and_3_out, and_4_out);
  or or_2 (loadA, instruction[15], selInstrOrALU);
  and and_8 (loadPC, isCinstruction, isJump__unused);
  not not_4 (PCinc, loadPC);
  ALU alu_1 (
    .x(outDReg), .y(outAorM), .zx(instruction[11]), .nx(instruction[10]), .zy(instruction[9]),
    .ny(instruction[8]), .f(instruction[7]), .no(instruction[6]), .out(outM), .zr(zr), .ng(ng));

  // Other names for the same wires on the sheet: destIsM = instruction[3]; destIsD = instruction[4];
  //   destIsA = instruction[5]; no = instruction[6]; f = instruction[7]; ny = instruction[8]; zy = instruction[9];
  //   nx = instruction[10]; zx = instruction[11]; aBit = instruction[12]; isAinstruction = instruction[15];
  //   outALU[15:0] = outM; outAReg[14:0] = addressM; outPC[14:0] = pc

  // Notes on the sheet:
  //   CONTROL LOGIC
endmodule

// RAM
module Memory (
  input  [15:0] in,
  input  [15:0] outKeyboard,
  input  clk,
  input  load,
  input  [14:0] address,
  output [15:0] out
);

  wire dmux4way_1_a, dmux4way_1_b, selRAM, selScreen;
  wire [15:0] outRAM, outScreen;

  DMux4Way dmux4way_1 (.in(load), .sel(address[14:13]), .a(dmux4way_1_a), .b(dmux4way_1_b), .c(selScreen));  // open: d
  or or_1 (selRAM, dmux4way_1_a, dmux4way_1_b);
  Mux4Way16 mux4way16_1 (.a(outRAM), .b(outRAM), .c(outScreen), .d(outKeyboard), .sel(address[14:13]), .out(out));
  RAM #(.addrWidth(14), .dataWidth(16), .bus("separate")) ram_1 (
    .addr(address[13:0]), .din(in), .data(outRAM), .str(selRAM), .clk(clk), .ld(1'b1));  // open: sel, clr
  RAM #(.addrWidth(13), .dataWidth(16), .bus("separate")) ram_2 (
    .addr(address[12:0]), .din(in), .data(outScreen), .str(selScreen), .clk(clk), .ld(1'b1));  // open: sel, clr
endmodule
