// Logisim project cpu7400.circ as structural Verilog: 15 circuits, main circuit Computer
module Computer (
  input  reset
);

  wire clk, cpu_1_writem;
  wire [14:0] cpu_1_addressm, cpu_1_pc;
  wire [15:0] cpu_1_outm, memory_1_out, rom_1_data, undriven;

  Clock clock_1 (.out(clk));
  ROM #(.addrWidth(15), .dataWidth(16)) rom_1 (.addr(cpu_1_pc), .data(rom_1_data));  // open: sel
  Keyboard keyboard_1 (.clk(clk));  // open: re, clr, avail, data
  CPU cpu_1 (
    .inM(memory_1_out), .instruction(rom_1_data), .reset(reset), .clk(clk), .outM(cpu_1_outm),
    .writeM(cpu_1_writem), .addressM(cpu_1_addressm), .pc(cpu_1_pc));
  Memory memory_1 (
    .in(cpu_1_outm), .outKeyboard(undriven), .clk(clk), .load(cpu_1_writem), .address(cpu_1_addressm),
    .out(memory_1_out));
endmodule

module CPU (
  input  reset,
  input  clk,
  input  [15:0] inM,
  input  [15:0] instruction,
  output [15:0] outM,
  output writeM,
  output [14:0] addressM,
  output [14:0] pc
);

  wire and_2_out, and_3_out, and_4_out, isCinstruction, isJump__unused, isPositive__unused, loadA, loadD,
       loadPC, ng, not_2_out, not_3_out, PCinc, selInstrOrALU, zr;
  wire [15:0] mux16_1_out, outAorM, outDReg;
  wire [15:15] outAReg, outPC;

  Mux16 mux16_1 (.sel(selInstrOrALU), .a(instruction), .b(outM), .out(mux16_1_out));
  not not_1 (isCinstruction, instruction[15]);
  Register A (.load(loadA), .clk(clk), .a(mux16_1_out), .out_4({outAReg[15], addressM}));
  Register D (.load(loadD), .clk(clk), .a(outM), .out_4(outDReg));
  PC pc_1 (.load(loadPC), .inc(PCinc), .reset(reset), .clk(clk), .a({outAReg[15], addressM}), .out_6({outPC[15], pc}));
  Mux16 mux16_2 (.sel(instruction[12]), .a({outAReg[15], addressM}), .b(inM), .out(outAorM));
  not not_2 (not_2_out, zr);
  and and_1 (isPositive__unused, not_2_out, not_3_out);
  not not_3 (not_3_out, ng);
  and and_2 (and_2_out, isPositive__unused, instruction[0]);
  and and_3 (and_3_out, zr, instruction[1]);
  and and_4 (and_4_out, ng, instruction[2]);
  and and_5 (selInstrOrALU, instruction[5], isCinstruction);
  and and_6 (loadD, instruction[4], isCinstruction);
  and and_7 (writeM, isCinstruction, instruction[3]);
  or or_1 (isJump__unused, and_2_out, and_3_out, and_4_out);
  or or_2 (loadA, instruction[15], selInstrOrALU);
  and and_8 (loadPC, isCinstruction, isJump__unused);
  not not_4 (PCinc, loadPC);
  ALU alu_1 (
    .x(outDReg), .y(outAorM), .zx(instruction[11]), .nx(instruction[10]), .zy(instruction[9]),
    .ny(instruction[8]), .f(instruction[7]), .no(instruction[6]), .out(outM), .zr(zr), .ng(ng));

  // Other names for the same wires on the sheet: destIsM = instruction[3]; destIsD = instruction[4];
  //   destIsA = instruction[5]; no = instruction[6]; f = instruction[7]; ny = instruction[8]; zy = instruction[9];
  //   nx = instruction[10]; zx = instruction[11]; aBit = instruction[12]; isAinstruction = instruction[15];
  //   outALU[15:0] = outM; outAReg[14:0] = addressM; outPC[14:0] = pc

  // Notes on the sheet:
  //   CONTROL LOGIC
endmodule

// RAM
module Memory (
  input  [15:0] in,
  input  [15:0] outKeyboard,
  input  clk,
  input  load,
  input  [14:0] address,
  output [15:0] out
);

  wire dmux4way_1_a, dmux4way_1_b, selRAM, selScreen;
  wire [15:0] outRAM, outScreen;

  DMux4Way dmux4way_1 (.in(load), .sel(address[14:13]), .a(dmux4way_1_a), .b(dmux4way_1_b), .c(selScreen));  // open: d
  or or_1 (selRAM, dmux4way_1_a, dmux4way_1_b);
  // Mux4Way16 mux4way16_1: pin names not known; wires that end beside it: outRAM, outRAM, outScreen, outKeyboard, address[14:13], out
  RAM #(.addrWidth(14), .dataWidth(16), .bus("separate")) ram_1 (
    .addr(address[13:0]), .din(in), .data(outRAM), .str(selRAM), .clk(clk), .ld(1'b1));  // open: sel, clr
  RAM #(.addrWidth(13), .dataWidth(16), .bus("separate")) ram_2 (
    .addr(address[12:0]), .din(in), .data(outScreen), .str(selScreen), .clk(clk), .ld(1'b1));  // open: sel, clr
endmodule

module ALU (
  input  [15:0] x,
  input  [15:0] y,
  input  zx,
  input  nx,
  input  zy,
  input  ny,
  input  f,
  input  no,
  output [15:0] out,
  output zr,
  output ng
);

  wire or8way_1_out, or8way_2_out;
  wire [15:0] add16_1_out_3, and16_1_out_3, bit_extender_1_out, bit_extender_2_out, bit_extender_3_out,
       mux16_1_out, mux16_2_out, mux16_3_out, xor16_1_out_3, xor16_2_out_3;

  assign bit_extender_1_out = {{15{nx}}, nx};  // Bit_Extender bit_extender_1
  Mux16 mux16_1 (.sel(zx), .a(x), .b({16{1'b0}}), .out(mux16_1_out));
  assign bit_extender_2_out = {{15{ny}}, ny};  // Bit_Extender bit_extender_2
  Mux16 mux16_2 (.sel(zy), .a(y), .b({16{1'b0}}), .out(mux16_2_out));
  XOR16 xor16_1 (.a(bit_extender_1_out), .b(mux16_1_out), .out_3(xor16_1_out_3));
  XOR16 xor16_2 (.a(bit_extender_2_out), .b(mux16_2_out), .out_3(xor16_2_out_3));
  And16 and16_1 (.a(xor16_1_out_3), .b(xor16_2_out_3), .out_3(and16_1_out_3));
  Add16 add16_1 (.a(xor16_1_out_3), .b(xor16_2_out_3), .out_3(add16_1_out_3));
  Mux16 mux16_3 (.sel(f), .a(and16_1_out_3), .b(add16_1_out_3), .out(mux16_3_out));
  assign bit_extender_3_out = {{15{no}}, no};  // Bit_Extender bit_extender_3
  XOR16 xor16_3 (.a(bit_extender_3_out), .b(mux16_3_out), .out_3({ng, out[14:0]}));
  Or8Way or8way_1 (.in(out[7:0]), .out(or8way_1_out));
  Or8Way or8way_2 (.in({ng, out[14:8]}), .out(or8way_2_out));
  nor nor_1 (zr, or8way_1_out, or8way_2_out);

  assign out[15] = ng;

  // Notes on the sheet:
  //   x input
  //   y input
endmodule

module PC (
  input  load,
  input  inc,
  input  reset,
  input  clk,
  input  [15:0] a,
  output [15:0] out_6
);

  wire load_t, n74163_1__15__tc, n74163_2__15__tc, n74163_3__15__tc, reset_t, tc3;

  not not_1 (load_t, load);
  not not_2 (reset_t, reset);
  _74163 u_74163_1 (
    ._1__nMR(reset_t), ._2__CP(clk), ._3__D0(a[0]), ._4__D1(a[1]), ._5__D2(a[2]), ._6__D3(a[3]),
    ._7__CEP(inc), ._8__GND(1'b0), ._16__Vcc(1'b1), ._15__TC(n74163_1__15__tc), ._14__Q0(out_6[0]),
    ._13__Q1(out_6[1]), ._12__Q2(out_6[2]), ._11__O3(out_6[3]), ._10__CET(inc), ._9__nPE(load_t));
  _74163 u_74163_2 (
    ._1__nMR(reset_t), ._2__CP(clk), ._3__D0(a[4]), ._4__D1(a[5]), ._5__D2(a[6]), ._6__D3(a[7]),
    ._8__GND(1'b0), ._16__Vcc(1'b1), ._15__TC(n74163_2__15__tc), ._14__Q0(out_6[4]), ._13__Q1(out_6[5]),
    ._12__Q2(out_6[6]), ._11__O3(out_6[7]), ._10__CET(n74163_1__15__tc), ._9__nPE(load_t));  // open: _7__CEP
  _74163 u_74163_3 (
    ._1__nMR(reset_t), ._2__CP(clk), ._3__D0(a[8]), ._4__D1(a[9]), ._5__D2(a[10]), ._6__D3(a[11]),
    ._8__GND(1'b0), ._16__Vcc(1'b1), ._15__TC(n74163_3__15__tc), ._14__Q0(out_6[8]), ._13__Q1(out_6[9]),
    ._12__Q2(out_6[10]), ._11__O3(out_6[11]), ._10__CET(n74163_2__15__tc), ._9__nPE(load_t));  // open: _7__CEP
  _74163 u_74163_4 (
    ._1__nMR(reset_t), ._2__CP(clk), ._3__D0(a[12]), ._4__D1(a[13]), ._5__D2(a[14]), ._6__D3(a[15]),
    ._8__GND(1'b0), ._16__Vcc(1'b1), ._15__TC(tc3), ._14__Q0(out_6[12]), ._13__Q1(out_6[13]),
    ._12__Q2(out_6[14]), ._11__O3(out_6[15]), ._10__CET(n74163_3__15__tc), ._9__nPE(load_t));  // open: _7__CEP

  // Other names for the same wires on the sheet: out0 = out_6[0]; out1 = out_6[1]; out2 = out_6[2]; out3 = out_6[3];
  //   out4 = out_6[4]; out5 = out_6[5]; out6 = out_6[6]; out7 = out_6[7]; out8 = out_6[8]; out9 = out_6[9];
  //   out10 = out_6[10]; out11 = out_6[11]; out12 = out_6[12]; out13 = out_6[13]; out14 = out_6[14];
  //   out15 = out_6[15]
endmodule

module Register (
  input  load,
  input  clk,
  input  [15:0] a,
  output [15:0] out_4
);

  wire clk_t;

  and and_1 (clk_t, load, clk);
  IC_74273 ic_74273_1 (
    .CLK(clk_t), .D1(a[0]), .D2(a[1]), .D3(a[2]), .D4(a[3]), .D5(a[4]), .D6(a[5]), .D7(a[6]), .D8(a[7]),
    .Y1(out_4[0]), .Y2(out_4[1]), .Y3(out_4[2]), .Y4(out_4[3]), .Y6(out_4[5]), .Y7(out_4[6]), .Y8(out_4[7]),
    .Y5(out_4[4]), .Vcc(1'b1), .GND(1'b0));  // open: CLR
  IC_74273 ic_74273_2 (
    .CLK(clk_t), .D1(a[8]), .D2(a[9]), .D3(a[10]), .D4(a[11]), .D5(a[12]), .D6(a[13]), .D7(a[14]),
    .D8(a[15]), .Y1(out_4[8]), .Y2(out_4[9]), .Y3(out_4[10]), .Y4(out_4[11]), .Y6(out_4[13]), .Y7(out_4[14]),
    .Y8(out_4[15]), .Y5(out_4[12]), .Vcc(1'b1), .GND(1'b0));  // open: CLR

  // Other names for the same wires on the sheet: out0 = out_4[0]; out1 = out_4[1]; out2 = out_4[2]; out3 = out_4[3];
  //   out4 = out_4[4]; out5 = out_4[5]; out6 = out_4[6]; out7 = out_4[7]; out8 = out_4[8]; out9 = out_4[9];
  //   out10 = out_4[10]; out11 = out_4[11]; out12 = out_4[12]; out13 = out_4[13]; out14 = out_4[14];
  //   out15 = out_4[15]
endmodule

// Add
module Add16 (
  input  [15:0] a,
  input  [15:0] b,
  output [15:0] out_3
);

  wire n7483_1__14__cout, n7483_2__14__cout, n7483_3__14__cout, n7483_4__14__cout;

  _7483 u_7483_1 (
    ._1__A4(a[3]), ._2__S3(out_3[2]), ._3__A3(a[2]), ._4__B3(b[2]), ._5__Vcc(1'b1), ._6__S2(out_3[1]),
    ._7__B2(b[1]), ._8__A2(a[1]), ._16__B4(b[3]), ._15__S4(out_3[3]), ._14__Cout(n7483_1__14__cout),
    ._13__Cin(1'b0), ._12__GND(1'b0), ._11__B1(b[0]), ._10__A1(a[0]), ._9__S1(out_3[0]));
  _7483 u_7483_2 (
    ._1__A4(a[7]), ._2__S3(out_3[6]), ._3__A3(a[6]), ._4__B3(b[6]), ._5__Vcc(1'b1), ._6__S2(out_3[5]),
    ._7__B2(b[5]), ._8__A2(a[5]), ._16__B4(b[7]), ._15__S4(out_3[7]), ._14__Cout(n7483_2__14__cout),
    ._13__Cin(n7483_1__14__cout), ._12__GND(1'b0), ._11__B1(b[4]), ._10__A1(a[4]), ._9__S1(out_3[4]));
  _7483 u_7483_3 (
    ._1__A4(a[11]), ._2__S3(out_3[10]), ._3__A3(a[10]), ._4__B3(b[10]), ._5__Vcc(1'b1), ._6__S2(out_3[9]),
    ._7__B2(b[9]), ._8__A2(a[9]), ._16__B4(b[11]), ._15__S4(out_3[11]), ._14__Cout(n7483_3__14__cout),
    ._13__Cin(n7483_2__14__cout), ._12__GND(1'b0), ._11__B1(b[8]), ._10__A1(a[8]), ._9__S1(out_3[8]));
  _7483 u_7483_4 (
    ._1__A4(a[15]), ._2__S3(out_3[14]), ._3__A3(a[14]), ._4__B3(b[14]), ._5__Vcc(1'b1), ._6__S2(out_3[13]),
    ._7__B2(b[13]), ._8__A2(a[13]), ._16__B4(b[15]), ._15__S4(out_3[15]), ._14__Cout(n7483_4__14__cout),
    ._13__Cin(n7483_3__14__cout), ._12__GND(n7483_4__14__cout), ._11__B1(b[12]), ._10__A1(a[12]),
    ._9__S1(out_3[12]));
  // also tied to GND on the sheet: n7483_4__14__cout

  // Other names for the same wires on the sheet: out0 = out_3[0]; out1 = out_3[1]; out2 = out_3[2]; out3 = out_3[3];
  //   out4 = out_3[4]; out5 = out_3[5]; out6 = out_3[6]; out7 = out_3[7]; out8 = out_3[8]; out9 = out_3[9];
  //   out10 = out_3[10]; out11 = out_3[11]; out12 = out_3[12]; out13 = out_3[13]; out14 = out_3[14];
  //   out15 = out_3[15]
endmodule

module FullAdder (
  input  a,
  input  b,
  input  c,
  output sum,
  output carry
);

  wire halfadder_1_carry, halfadder_1_sum, halfadder_2_carry;

  HalfAdder halfadder_1 (.a(a), .b(b), .sum(halfadder_1_sum), .carry(halfadder_1_carry));
  HalfAdder halfadder_2 (.a(halfadder_1_sum), .b(c), .sum(sum), .carry(halfadder_2_carry));
  or or_1 (carry, halfadder_2_carry, halfadder_1_carry);
endmodule

module HalfAdder (
  input  a,
  input  b,
  output sum,
  output carry
);

  xor xor_1 (sum, a, b);
  and and_1 (carry, a, b);
endmodule

// Mux
module Mux16 (
  input  sel,
  input  [15:0] a,
  input  [15:0] b,
  output [15:0] out
);

  _74157 u_74157_1 (
    ._1__S(sel), ._2__A1(a[0]), ._3__B1(b[0]), ._4__Y1(out[0]), ._5__A2(a[1]), ._6__B2(b[1]),
    ._7__Y2(out[1]), ._8__GND(1'b0), ._16__Vcc(1'b1), ._15__G(1'b0), ._14__A4(a[3]), ._13__B4(b[3]),
    ._12__Y4(out[3]), ._11__A3(a[2]), ._10__B3(b[2]), ._9__Y3(out[2]));
  _74157 u_74157_2 (
    ._1__S(sel), ._2__A1(a[4]), ._3__B1(b[4]), ._4__Y1(out[4]), ._5__A2(a[5]), ._6__B2(b[5]),
    ._7__Y2(out[5]), ._8__GND(1'b0), ._16__Vcc(1'b1), ._15__G(1'b0), ._14__A4(a[7]), ._13__B4(b[7]),
    ._12__Y4(out[7]), ._11__A3(a[6]), ._10__B3(b[6]), ._9__Y3(out[6]));
  _74157 u_74157_3 (
    ._1__S(sel), ._2__A1(a[8]), ._3__B1(b[8]), ._4__Y1(out[8]), ._5__A2(a[9]), ._6__B2(b[9]),
    ._7__Y2(out[9]), ._8__GND(1'b0), ._16__Vcc(1'b1), ._15__G(1'b0), ._14__A4(a[11]), ._13__B4(b[11]),
    ._12__Y4(out[11]), ._11__A3(a[10]), ._10__B3(b[10]), ._9__Y3(out[10]));
  _74157 u_74157_4 (
    ._1__S(sel), ._2__A1(a[12]), ._3__B1(b[12]), ._4__Y1(out[12]), ._5__A2(a[13]), ._6__B2(b[13]),
    ._7__Y2(out[13]), ._8__GND(1'b0), ._16__Vcc(1'b1), ._15__G(1'b0), ._14__A4(a[15]), ._13__B4(b[15]),
    ._12__Y4(out[15]), ._11__A3(a[14]), ._10__B3(b[14]), ._9__Y3(out[14]));
endmodule

module Mux4Way16 (
  input  [15:0] a,
  input  [15:0] b,
  input  [15:0] c,
  input  [15:0] d,
  input  [1:0] sel,
  output [15:0] out
);

  wire [15:0] mux16_1_out, mux16_2_out;

  Mux16 mux16_1 (.sel(sel[0]), .a(a), .b(b), .out(mux16_1_out));
  Mux16 mux16_2 (.sel(sel[0]), .a(c), .b(d), .out(mux16_2_out));
  Mux16 mux16_3 (.sel(sel[1]), .a(mux16_1_out), .b(mux16_2_out), .out(out));
endmodule

module DMux4Way (
  input  in,
  input  [1:0] sel,
  output a,
  output b,
  output c,
  output d
);

  Demultiplexer #(.select(2), .enable("false")) demultiplexer_1 (
    .out0(a), .out1(b), .out2(c), .out3(d), .in(in), .sel(sel));
endmodule

// And
module And16 (
  input  [15:0] a,
  input  [15:0] b,
  output [15:0] out_3
);

  _7408 u_7408_1 (
    ._1__1A(a[0]), ._2__1B(b[0]), ._3__1Y(out_3[0]), ._4__2A(a[1]), ._5__2B(b[1]), ._6__2Y(out_3[1]),
    ._7__GND(1'b0), ._14__Vcc(1'b1), ._13__4B(b[3]), ._12__4A(a[3]), ._11__4Y(out_3[3]), ._10__3B(b[2]),
    ._9__3A(a[2]), ._8__3Y(out_3[2]));
  _7408 u_7408_2 (
    ._1__1A(a[4]), ._2__1B(b[4]), ._3__1Y(out_3[4]), ._4__2A(a[5]), ._5__2B(b[5]), ._6__2Y(out_3[5]),
    ._7__GND(1'b0), ._14__Vcc(1'b1), ._13__4B(b[7]), ._12__4A(a[7]), ._11__4Y(out_3[7]), ._10__3B(b[6]),
    ._9__3A(a[6]), ._8__3Y(out_3[6]));
  _7408 u_7408_3 (
    ._1__1A(a[8]), ._2__1B(b[8]), ._3__1Y(out_3[8]), ._4__2A(a[9]), ._5__2B(b[9]), ._6__2Y(out_3[9]),
    ._7__GND(1'b0), ._14__Vcc(1'b1), ._13__4B(b[11]), ._12__4A(a[11]), ._11__4Y(out_3[11]), ._10__3B(b[10]),
    ._9__3A(a[10]), ._8__3Y(out_3[10]));
  _7408 u_7408_4 (
    ._1__1A(a[12]), ._2__1B(b[12]), ._3__1Y(out_3[12]), ._4__2A(a[13]), ._5__2B(b[13]), ._6__2Y(out_3[13]),
    ._7__GND(1'b0), ._14__Vcc(1'b1), ._13__4B(b[15]), ._12__4A(a[15]), ._11__4Y(out_3[15]), ._10__3B(b[14]),
    ._9__3A(a[14]), ._8__3Y(out_3[14]));

  // Other names for the same wires on the sheet: out0 = out_3[0]; out1 = out_3[1]; out2 = out_3[2]; out3 = out_3[3];
  //   out4 = out_3[4]; out5 = out_3[5]; out6 = out_3[6]; out7 = out_3[7]; out8 = out_3[8]; out9 = out_3[9];
  //   out10 = out_3[10]; out11 = out_3[11]; out12 = out_3[12]; out13 = out_3[13]; out14 = out_3[14];
  //   out15 = out_3[15]
endmodule

// Or
module Or8Way (
  input  [7:0] in,
  output out
);

  wire n7432_1__3__1y, n7432_1__6__2y, n7432_1__8__3y, n7432_1__11__4y, n7432_2__3__1y, n7432_2__11__4y;

  _7432 u_7432_1 (
    ._1__1A(in[0]), ._2__1B(in[1]), ._3__1Y(n7432_1__3__1y), ._4__2A(in[2]), ._5__2B(in[3]),
    ._6__2Y(n7432_1__6__2y), ._7__GND(1'b0), ._14__Vcc(1'b1), ._13__4B(in[7]), ._12__4A(in[6]),
    ._11__4Y(n7432_1__11__4y), ._10__3B(in[5]), ._9__3A(in[4]), ._8__3Y(n7432_1__8__3y));
  _7432 u_7432_2 (
    ._1__1A(n7432_1__6__2y), ._2__1B(n7432_1__3__1y), ._3__1Y(n7432_2__3__1y), ._4__2A(n7432_2__3__1y),
    ._5__2B(n7432_2__11__4y), ._6__2Y(out), ._7__GND(1'b0), ._14__Vcc(1'b1), ._13__4B(n7432_1__8__3y),
    ._12__4A(n7432_1__11__4y), ._11__4Y(n7432_2__11__4y));  // open: _10__3B, _9__3A, _8__3Y
endmodule

// XOR
module XOR16 (
  input  [15:0] a,
  input  [15:0] b,
  output [15:0] out_3
);

  _7486 u_7486_1 (
    ._1__1A(a[0]), ._2__1B(b[0]), ._3__1Y(out_3[0]), ._4__2A(a[1]), ._5__2B(b[1]), ._6__2Y(out_3[1]),
    ._7__GND(1'b0), ._14__Vcc(1'b1), ._13__4B(b[3]), ._12__4A(a[3]), ._11__4Y(out_3[3]), ._10__3B(b[2]),
    ._9__3A(a[2]), ._8__3Y(out_3[2]));
  _7486 u_7486_2 (
    ._1__1A(a[4]), ._2__1B(b[4]), ._3__1Y(out_3[4]), ._4__2A(a[5]), ._5__2B(b[5]), ._6__2Y(out_3[5]),
    ._7__GND(1'b0), ._14__Vcc(1'b1), ._13__4B(b[7]), ._12__4A(a[7]), ._11__4Y(out_3[7]), ._10__3B(b[6]),
    ._9__3A(a[6]), ._8__3Y(out_3[6]));
  _7486 u_7486_3 (
    ._1__1A(a[8]), ._2__1B(b[8]), ._3__1Y(out_3[8]), ._4__2A(a[9]), ._5__2B(b[9]), ._6__2Y(out_3[9]),
    ._7__GND(1'b0), ._14__Vcc(1'b1), ._13__4B(b[11]), ._12__4A(a[11]), ._11__4Y(out_3[11]), ._10__3B(b[10]),
    ._9__3A(a[10]), ._8__3Y(out_3[10]));
  _7486 u_7486_4 (
    ._1__1A(a[12]), ._2__1B(b[12]), ._3__1Y(out_3[12]), ._4__2A(a[13]), ._5__2B(b[13]), ._6__2Y(out_3[13]),
    ._7__GND(1'b0), ._14__Vcc(1'b1), ._13__4B(b[15]), ._12__4A(a[15]), ._11__4Y(out_3[15]), ._10__3B(b[14]),
    ._9__3A(a[14]), ._8__3Y(out_3[14]));

  // Other names for the same wires on the sheet: out0 = out_3[0]; out1 = out_3[1]; out2 = out_3[2]; out3 = out_3[3];
  //   out4 = out_3[4]; out5 = out_3[5]; out6 = out_3[6]; out7 = out_3[7]; out8 = out_3[8]; out9 = out_3[9];
  //   out10 = out_3[10]; out11 = out_3[11]; out12 = out_3[12]; out13 = out_3[13]; out14 = out_3[14];
  //   out15 = out_3[15]
endmodule
